// Logisim project cpu.circ as structural Verilog: 1 circuit, main circuit main
module main (
);

  wire adder_1_cout, AI, and_2_out, and_3_out, AO, buffer_3_out, C, CA, CE, CF, CHO, CI, CLO, CO,
       controlled_inverter_1_out, decoder_1_out0, decoder_1_out1, decoder_1_out2, decoder_1_out3,
       decoder_1_out4, decoder_1_out5, decoder_1_out6, decoder_1_out7, decoder_1_out8, decoder_1_out9,
       decoder_1_out10, decoder_1_out11, decoder_1_out12, decoder_1_out13, decoder_1_out14, decoder_1_out15,
       demultiplexer_1_out1, demultiplexer_1_out2, demultiplexer_1_out3, demultiplexer_1_out4,
       demultiplexer_1_out5, demultiplexer_2_out1, demultiplexer_2_out2, demultiplexer_2_out3,
       demultiplexer_2_out4, demultiplexer_2_out5, DONE, FI, HI, HLMI, HLMO, HLT, HMI, HO, IR0I, IR1I, IR1O,
       IR2I, IR2O, IRI, LI, LMI, LO, MI, MO, nor_1_out, nor_2_out, nor_3_out, nor_4_out, not_1_out, or_1_out,
       or_2_out, or_3_out, or_4_out, pull_resistor_6_node, RI, RO, RSE, RST, SO, SPD, SPI, SPO,
       subtractor_1_bout, TMI, TMO, ZF;
  wire [1:0] and_4_out, controlled_buffer_1_out_3;
  wire [2:0] controlled_buffer_1_out, controlled_buffer_1_out_2, register_2_q, SS;
  wire [3:0] counter_1_q, ROM1_data;
  wire [7:0] A_q, adder_1_out, and_1_out, B_q, C_q, controlled_buffer_6_out, controlled_buffer_6_out_2, D_q,
       E_q, F_q, H_q, HMAR_q, IR1_q, IR2_q, L_q, LMAR_q, multiplexer_1_out, negator_1_out, OPCODE, or_5_out,
       ram_1_dout, register_1_q, S_q, shifter_1_out, shifter_2_out, subtractor_1_out, xor_1_out;
  wire [7:2] FL_q;
  wire [7:3] ROM2_data;
  wire [7:4] ROM1_data_2;
  wire [11:11] pull_resistor_4_node;
  wire [15:0] PC_q, SP_q;

  LED led_1 (.in(decoder_1_out0));
  LED led_2 (.in(decoder_1_out1));
  LED led_3 (.in(decoder_1_out2));
  LED led_4 (.in(decoder_1_out3));
  ROM #(.addrWidth(12)) ROM1 (
    .addr({pull_resistor_4_node[11], CF, ZF, counter_1_q, OPCODE[4:0]}), .data({ROM1_data_2, ROM1_data}));
  LED led_5 (.in(decoder_1_out5));
  LED led_6 (.in(decoder_1_out6));
  LED led_7 (.in(decoder_1_out7));
  LED led_8 (.in(decoder_1_out4));
  Button RESET (.out(RST));
  Pull_Resistor pull_resistor_1 (.node(RST));
  Register IR0 (
    .D({controlled_buffer_1_out_3, controlled_buffer_1_out_2, controlled_buffer_1_out}), .en(IR0I), .clk(C),
    .Q(OPCODE), .clr(RST));
  Register IR1 (
    .D({controlled_buffer_1_out_3, controlled_buffer_1_out_2, controlled_buffer_1_out}), .en(IR1I), .clk(C),
    .Q(IR1_q), .clr(RST));
  Register IR2 (
    .D({controlled_buffer_1_out_3, controlled_buffer_1_out_2, controlled_buffer_1_out}), .en(IR2I), .clk(C),
    .Q(IR2_q), .clr(RST));
  Counter #(.max('hffff), .width(16)) PC (
    .clr(RST), .load(CI), .count(CE), .clk(C), .D({controlled_buffer_6_out_2, controlled_buffer_6_out}),
    .Q(PC_q));  // open: up, carry
  assign {controlled_buffer_1_out_3, controlled_buffer_1_out_2, controlled_buffer_1_out} = CLO ? controlled_buffer_6_out : 8'bz;  // Controlled_Buffer controlled_buffer_1
  assign {controlled_buffer_1_out_3, controlled_buffer_1_out_2, controlled_buffer_1_out} = CHO ? controlled_buffer_6_out_2 : 8'bz;  // Controlled_Buffer controlled_buffer_2
  Clock clock_1 (.out(C));
  LED led_9 (.in(decoder_1_out8));
  LED led_10 (.in(decoder_1_out9));
  LED led_11 (.in(decoder_1_out10));
  LED led_12 (.in(decoder_1_out11));
  Decoder #(.enable("false"), .select(4)) decoder_1 (
    .out0(decoder_1_out0), .out1(decoder_1_out1), .out2(decoder_1_out2), .out3(decoder_1_out3),
    .out4(decoder_1_out4), .out5(decoder_1_out5), .out6(decoder_1_out6), .out7(decoder_1_out7),
    .out8(decoder_1_out8), .out9(decoder_1_out9), .out10(decoder_1_out10), .out11(decoder_1_out11),
    .out12(decoder_1_out12), .out13(decoder_1_out13), .out14(decoder_1_out14), .out15(decoder_1_out15),
    .sel(counter_1_q));
  Decoder #(.enable("false"), .select(4)) decoder_2 (
    .out1(AI), .out2(HI), .out3(LI), .out4(RI), .out5(TMI), .out6(MI), .out7(CI), .out8(RSE), .out9(IR0I),
    .out10(IR1I), .out11(IR2I), .out12(HLMI), .out13(LMI), .out14(HMI), .sel(ROM1_data));  // open: out0, out15
  Register register_1 (
    .D({controlled_buffer_1_out_3, controlled_buffer_1_out_2, controlled_buffer_1_out}), .en(TMI), .clk(C),
    .Q(register_1_q), .clr(RST));
  assign {controlled_buffer_1_out_3, controlled_buffer_1_out_2, controlled_buffer_1_out} = IR1O ? IR1_q : 8'bz;  // Controlled_Buffer controlled_buffer_3
  assign {controlled_buffer_1_out_3, controlled_buffer_1_out_2, controlled_buffer_1_out} = IR2O ? IR2_q : 8'bz;  // Controlled_Buffer controlled_buffer_4
  LED led_13 (.in(decoder_1_out12));
  LED led_14 (.in(decoder_1_out13));
  LED led_15 (.in(decoder_1_out14));
  LED led_16 (.in(decoder_1_out15));
  // Probe on {pull_resistor_4_node[11], CF, ZF, counter_1_q, OPCODE[4:0]}
  assign {controlled_buffer_1_out_3, controlled_buffer_1_out_2, controlled_buffer_1_out} = TMO ? register_1_q : 8'bz;  // Controlled_Buffer controlled_buffer_5
  Register #(.width(3)) register_2 (.D(controlled_buffer_1_out), .en(RSE), .clk(C), .Q(register_2_q), .clr(RST));
  Demultiplexer #(.select(3)) demultiplexer_1 (
    .out0(AI), .out1(demultiplexer_1_out1), .out2(demultiplexer_1_out2), .out3(demultiplexer_1_out3),
    .out4(demultiplexer_1_out4), .out5(demultiplexer_1_out5), .out6(HI), .out7(LI), .in(IRI),
    .sel(register_2_q));
  not not_1 (not_1_out, HLT);
  assign controlled_inverter_1_out = not_1_out ? ~C : 1'bz;  // Controlled_Inverter controlled_inverter_1
  Pull_Resistor pull_resistor_2 (.node(controlled_inverter_1_out));
  Counter #(.max('hf), .width(4)) counter_1 (
    .clr(or_1_out), .clk(controlled_inverter_1_out), .Q(counter_1_q));  // open: load, up, count, D, carry
  or or_1 (or_1_out, DONE, RST);
  assign {controlled_buffer_6_out_2, controlled_buffer_6_out} = CO ? PC_q : 16'bz;  // Controlled_Buffer controlled_buffer_6
  assign {controlled_buffer_6_out_2, controlled_buffer_6_out} = SPO ? SP_q : 16'bz;  // Controlled_Buffer controlled_buffer_7
  // Probe on C
  ROM #(.addrWidth(12)) ROM2 (
    .addr({pull_resistor_4_node[11], CF, ZF, counter_1_q, OPCODE[4:0]}), .data({ROM2_data, SS}));
  // Probe on {controlled_buffer_1_out_3, controlled_buffer_1_out_2, controlled_buffer_1_out}
  Pull_Resistor pull_resistor_3 (.node({controlled_buffer_1_out_3, controlled_buffer_1_out_2, controlled_buffer_1_out}));
  assign controlled_buffer_6_out = {controlled_buffer_1_out_3, controlled_buffer_1_out_2, controlled_buffer_1_out};  // Buffer buffer_1, 8 bits wide
  or or_2 (or_2_out, LMI, HLMI);
  assign controlled_buffer_6_out_2 = {controlled_buffer_1_out_3, controlled_buffer_1_out_2, controlled_buffer_1_out};  // Buffer buffer_2, 8 bits wide
  or or_3 (or_3_out, HMI, HLMI);
  or or_4 (or_4_out, SPI, SPD);
  Decoder #(.enable("false"), .select(4)) decoder_3 (
    .out1(AO), .out2(HO), .out3(LO), .out4(RO), .out5(TMO), .out6(SO), .out7(IR1O), .out8(IR2O), .out9(MO),
    .out10(CO), .out11(HLMO), .out12(CLO), .out13(CHO), .sel(ROM1_data_2));  // open: out0, out14, out15
  Register A (
    .D({controlled_buffer_1_out_3, controlled_buffer_1_out_2, controlled_buffer_1_out}), .en(AI), .clk(C),
    .Q(A_q), .clr(RST));
  Register B (
    .D({controlled_buffer_1_out_3, controlled_buffer_1_out_2, controlled_buffer_1_out}),
    .en(demultiplexer_1_out1), .clk(C), .Q(B_q), .clr(RST));
  Register u_C (
    .D({controlled_buffer_1_out_3, controlled_buffer_1_out_2, controlled_buffer_1_out}),
    .en(demultiplexer_1_out2), .clk(C), .Q(C_q), .clr(RST));
  Register D (
    .D({controlled_buffer_1_out_3, controlled_buffer_1_out_2, controlled_buffer_1_out}),
    .en(demultiplexer_1_out3), .clk(C), .Q(D_q), .clr(RST));
  Register E (
    .D({controlled_buffer_1_out_3, controlled_buffer_1_out_2, controlled_buffer_1_out}),
    .en(demultiplexer_1_out4), .clk(C), .Q(E_q), .clr(RST));
  Register F (
    .D({controlled_buffer_1_out_3, controlled_buffer_1_out_2, controlled_buffer_1_out}),
    .en(demultiplexer_1_out5), .clk(C), .Q(F_q), .clr(RST));
  Register H (
    .D({controlled_buffer_1_out_3, controlled_buffer_1_out_2, controlled_buffer_1_out}), .en(HI), .clk(C),
    .Q(H_q), .clr(RST));
  Register L (
    .D({controlled_buffer_1_out_3, controlled_buffer_1_out_2, controlled_buffer_1_out}), .en(LI), .clk(C),
    .Q(L_q), .clr(RST));
  Register LMAR (.D(controlled_buffer_6_out), .en(or_2_out), .clk(C), .Q(LMAR_q), .clr(RST));
  Register HMAR (.D(controlled_buffer_6_out_2), .en(or_3_out), .clk(C), .Q(HMAR_q), .clr(RST));
  Counter #(.max('hffff), .ongoal("stay"), .width(16)) SP (
    .load(RST), .up(SPI), .count(or_4_out), .clk(C), .D({16{1'b1}}), .Q(SP_q));  // open: clr, carry
  buf buffer_3 (buffer_3_out, RO);
  Demultiplexer #(.select(3)) demultiplexer_2 (
    .out0(AO), .out1(demultiplexer_2_out1), .out2(demultiplexer_2_out2), .out3(demultiplexer_2_out3),
    .out4(demultiplexer_2_out4), .out5(demultiplexer_2_out5), .out6(HO), .out7(LO), .in(buffer_3_out),
    .sel(register_2_q));
  assign {controlled_buffer_1_out_3, controlled_buffer_1_out_2, controlled_buffer_1_out} = AO ? A_q : 8'bz;  // Controlled_Buffer controlled_buffer_8
  assign {controlled_buffer_1_out_3, controlled_buffer_1_out_2, controlled_buffer_1_out} = demultiplexer_2_out1 ? B_q : 8'bz;  // Controlled_Buffer controlled_buffer_9
  assign {controlled_buffer_1_out_3, controlled_buffer_1_out_2, controlled_buffer_1_out} = demultiplexer_2_out2 ? C_q : 8'bz;  // Controlled_Buffer controlled_buffer_10
  assign {controlled_buffer_1_out_3, controlled_buffer_1_out_2, controlled_buffer_1_out} = demultiplexer_2_out3 ? D_q : 8'bz;  // Controlled_Buffer controlled_buffer_11
  assign {controlled_buffer_1_out_3, controlled_buffer_1_out_2, controlled_buffer_1_out} = demultiplexer_2_out4 ? E_q : 8'bz;  // Controlled_Buffer controlled_buffer_12
  assign {controlled_buffer_1_out_3, controlled_buffer_1_out_2, controlled_buffer_1_out} = demultiplexer_2_out5 ? F_q : 8'bz;  // Controlled_Buffer controlled_buffer_13
  assign {controlled_buffer_1_out_3, controlled_buffer_1_out_2, controlled_buffer_1_out} = HO ? H_q : 8'bz;  // Controlled_Buffer controlled_buffer_14
  assign {controlled_buffer_1_out_3, controlled_buffer_1_out_2, controlled_buffer_1_out} = LO ? L_q : 8'bz;  // Controlled_Buffer controlled_buffer_15
  assign {controlled_buffer_6_out_2, controlled_buffer_6_out} = HLMO ? {HMAR_q, LMAR_q} : 16'bz;  // Controlled_Buffer controlled_buffer_16
  RAM #(.addrWidth(16), .\type ("nonvolatile")) ram_1 (
    .addr({HMAR_q, LMAR_q}), .we(MI), .oe(MO), .clk(C),
    .din({controlled_buffer_1_out_3, controlled_buffer_1_out_2, controlled_buffer_1_out}), .dout(ram_1_dout));
  Pull_Resistor pull_resistor_4 (.node(pull_resistor_4_node[11]));
  Decoder #(.enable("false"), .select(3)) decoder_4 (
    .out1(FI), .out2(CE), .out3(CA), .out4(SPO), .out5(SPI), .out6(SPD), .out7(DONE), .sel(ROM2_data[5:3]));  // open: out0
  Pull_Resistor pull_resistor_5 (.node(C));
  Adder adder_1 (
    .a(A_q), .b({controlled_buffer_1_out_3, controlled_buffer_1_out_2, controlled_buffer_1_out}),
    .out(adder_1_out), .cin(pull_resistor_6_node), .cout(adder_1_cout));
  Subtractor subtractor_1 (
    .a(A_q), .b({controlled_buffer_1_out_3, controlled_buffer_1_out_2, controlled_buffer_1_out}),
    .out(subtractor_1_out), .bin(pull_resistor_6_node), .bout(subtractor_1_bout));
  Shifter shifter_1 (.in(A_q), .\dist (3'b001), .out(shifter_1_out));
  Shifter #(.shift("ar")) shifter_2 (.in(A_q), .\dist (3'b001), .out(shifter_2_out));
  Negator negator_1 (.in(A_q), .out(negator_1_out));
  assign and_1_out = A_q & {controlled_buffer_1_out_3, controlled_buffer_1_out_2, controlled_buffer_1_out};  // AND_Gate and_1, 8 bits wide
  assign or_5_out = A_q | {controlled_buffer_1_out_3, controlled_buffer_1_out_2, controlled_buffer_1_out};  // OR_Gate or_5, 8 bits wide
  assign xor_1_out = A_q ^ {controlled_buffer_1_out_3, controlled_buffer_1_out_2, controlled_buffer_1_out};  // XOR_Gate xor_1, 8 bits wide
  assign {controlled_buffer_1_out_3, controlled_buffer_1_out_2, controlled_buffer_1_out} = MO ? ram_1_dout : 8'bz;  // Controlled_Buffer controlled_buffer_17
  or or_6 (and_4_out[1], adder_1_cout, subtractor_1_bout);
  Register S (.D(multiplexer_1_out), .en(RO), .clk(C), .Q(S_q), .clr(RST));
  Multiplexer #(.select(3), .width(8)) multiplexer_1 (
    .in0(adder_1_out), .in1(subtractor_1_out), .in2(shifter_1_out), .in3(shifter_2_out), .in4(negator_1_out),
    .in5(and_1_out), .in6(or_5_out), .in7(xor_1_out), .out(multiplexer_1_out), .sel(SS));
  Register FL (.D({{6{1'b0}}, and_4_out}), .en(FI), .clk(C), .Q({FL_q, CF, ZF}), .clr(RST));
  Register #(.width(1)) register_3 (.D(1'b1), .en(ROM2_data[6]), .clk(C), .Q(HLT), .clr(RST));
  assign {controlled_buffer_1_out_3, controlled_buffer_1_out_2, controlled_buffer_1_out} = SO ? S_q : 8'bz;  // Controlled_Buffer controlled_buffer_18
  nor nor_1 (nor_1_out, S_q[0], S_q[1]);
  and and_2 (and_2_out, nor_1_out, nor_2_out);
  nor nor_2 (nor_2_out, S_q[2], S_q[3]);
  nor nor_3 (nor_3_out, S_q[4], S_q[5]);
  and and_3 (and_3_out, nor_3_out, nor_4_out);
  nor nor_4 (nor_4_out, S_q[6], S_q[7]);
  Pull_Resistor pull_resistor_6 (.node(pull_resistor_6_node));
  and and_4 (and_4_out[0], and_2_out, and_3_out);
  assign pull_resistor_6_node = CA ? CF : 1'bz;  // Controlled_Buffer controlled_buffer_19

  // Notes on the sheet:
  //   contents of ROM1 (hex, n*v repeats v):
  //   27*ac 5*0 27*99 6*0 40 40 40 0 c c 20*ac 6*0 61 61 61 c 91 93 20*9a 9*0 16 0 c 8*78 7*ac 3d 78 ac 3d
  //   ac 11*0 92 8*40 7*9b 2e 84 9b 2e 9b 11*0 b7 4*61 0 61 61 61 0 7d 4*0 88 78 0 7d 78 7d 20*0 c 8e 4*0
  //   45 94 0 8e 46 8e 20*0 d6 b7 4*0 78 0 0 91 0 16 26*0 54 25*0 c 31*0 c6 31*0 7d 31*0 8e 31*0 b7 48*0
  //   27*ac 5*0 27*99 6*0 40 40 40 0 c c 20*ac 6*0 61 61 61 c 91 93 20*9a 9*0 16 0 c 8*78 7*ac 3d 78 ac 3d
  //   ac 11*0 92 8*40 7*9b 2e 84 9b 2e 9b 11*0 b7 4*61 0 61 61 61 0 7d 7d 7d 0 0 88 78 0 7d 78 7d 20*0 c
  //   8e 8e 8e 0 0 45 94 0 8e 46 8e 20*0 d6 b7 b7 b7 0 0 78 0 0 91 0 16 26*0 54 25*0 c 31*0 c6 31*0 7d
  //   31*0 8e 31*0 b7 48*0 27*ac 5*0 27*99 6*0 40 40 40 0 c c 20*ac 6*0 61 61 61 c 91 93 20*9a 9*0 16 0 c
  //   8*78 7*ac 3d 78 ac 3d ac 11*0 92 8*40 7*9b 2e 84 9b 2e 9b 11*0 b7 4*61 0 61 61 61 0 7d 0 0 7d 7d 88
  //   78 0 7d 78 7d 20*0 c 8e 0 0 8e 8e 45 94 0 8e 46 8e 20*0 d6 b7 0 0 b7 b7 78 0 0 91 0 16 26*0 54 25*0
  //   c 31*0 c6 31*0 7d 31*0 8e 31*0 b7 48*0 27*ac 5*0 27*99 6*0 40 40 40 0 c c 20*ac 6*0 61 61 61 c 91 93
  //   20*9a 9*0 16 0 c 8*78 7*ac 3d 78 ac 3d ac 11*0 92 8*40 7*9b 2e 84 9b 2e 9b 11*0 b7 4*61 0 61 61 61 0
  //   5*7d 88 78 0 7d 78 7d 20*0 c 5*8e 45 94 0 8e 46 8e 20*0 d6 5*b7 78 0 0 91 0 16 26*0 54 25*0 c 31*0
  //   c6 31*0 7d 31*0 8e 31*0 b7 48*0 27*ac 5*0 27*99 6*0 40 40 40 0 c c 20*ac 6*0 61 61 61 c 91 93 20*9a
  //   9*0 16 0 c 8*78 7*ac 3d 78 ac 3d ac 11*0 92 8*40 7*9b 2e 84 9b 2e 9b 11*0 b7 4*61 0 61 61 61 0 7d
  //   4*0 88 78 0 7d 78 7d 20*0 c 8e 4*0 45 94 0 8e 46 8e 20*0 d6 b7 4*0 78 0 0 91 0 16 26*0 54 25*0 c
  //   31*0 c6 31*0 7d 31*0 8e 31*0 b7 48*0 27*ac 5*0 27*99 6*0 40 40 40 0 c c 20*ac 6*0 61 61 61 c 91 93
  //   20*9a 9*0 16 0 c 8*78 7*ac 3d 78 ac 3d ac 11*0 92 8*40 7*9b 2e 84 9b 2e 9b 11*0 b7 4*61 0 61 61 61 0
  //   7d 7d 7d 0 0 88 78 0 7d 78 7d 20*0 c 8e 8e 8e 0 0 45 94 0 8e 46 8e 20*0 d6 b7 b7 b7 0 0 78 0 0 91 0
  //   16 26*0 54 25*0 c 31*0 c6 31*0 7d 31*0 8e 31*0 b7 48*0 27*ac 5*0 27*99 6*0 40 40 40 0 c c 20*ac 6*0
  //   61 61 61 c 91 93 20*9a 9*0 16 0 c 8*78 7*ac 3d 78 ac 3d ac 11*0 92 8*40 7*9b 2e 84 9b 2e 9b 11*0 b7
  //   4*61 0 61 61 61 0 7d 0 0 7d 7d 88 78 0 7d 78 7d 20*0 c 8e 0 0 8e 8e 45 94 0 8e 46 8e 20*0 d6 b7 0 0
  //   b7 b7 78 0 0 91 0 16 26*0 54 25*0 c 31*0 c6 31*0 7d 31*0 8e 31*0 b7 48*0 27*ac 5*0 27*99 6*0 40 40
  //   40 0 c c 20*ac 6*0 61 61 61 c 91 93 20*9a 9*0 16 0 c 8*78 7*ac 3d 78 ac 3d ac 11*0 92 8*40 7*9b 2e
  //   84 9b 2e 9b 11*0 b7 4*61 0 61 61 61 0 5*7d 88 78 0 7d 78 7d 20*0 c 5*8e 45 94 0 8e 46 8e 20*0 d6
  //   5*b7 78 0 0 91 0 16 26*0 54 25*0 c 31*0 c6 31*0 7d 31*0 8e 31*0 b7
  //   contents of ROM2 (hex, n*v repeats v):
  //   32*0 17*10 4*0 6*10 5*0 40 4 2 3 30 20 20 26*0 8 8 8 20 28 28 10*10 4*0 6*10 6*0 38 38 38 0 38 20
  //   29*0 38 0 28 0 18 1 19 1 5 6 7 10 10 4*0 10 0 0 10 0 10 12*0 8*8 30 7*0 38 14*0 9*38 20 38*0 38 0 0
  //   38 21*0 30 38 7*0 38 0 38 20*0 20 5*0 38 153*0 38 48*0 19*10 0 0 6*10 5*0 40 4 2 3 30 20 20 26*0 8 8
  //   8 20 28 28 12*10 0 0 6*10 6*0 38 38 38 0 38 20 29*0 38 0 28 0 18 1 19 1 5 6 7 4*10 0 0 10 0 0 10 0
  //   10 12*0 8*8 30 7*0 38 14*0 9*38 20 38*0 38 0 0 38 21*0 30 38 38 38 5*0 38 0 38 20*0 20 5*0 38 153*0
  //   38 48*0 17*10 0 0 8*10 5*0 40 4 2 3 30 20 20 26*0 8 8 8 20 28 28 10*10 0 0 8*10 6*0 38 38 38 0 38 20
  //   29*0 38 0 28 0 18 1 19 1 5 6 7 10 10 0 0 10 10 10 0 0 10 0 10 12*0 8*8 30 7*0 38 14*0 9*38 20 38*0
  //   38 0 0 38 21*0 30 38 0 0 38 38 0 0 0 38 0 38 20*0 20 5*0 38 153*0 38 48*0 27*10 5*0 40 4 2 3 30 20
  //   20 26*0 8 8 8 20 28 28 20*10 6*0 38 38 38 0 38 20 29*0 38 0 28 0 18 1 19 1 5 6 7 7*10 0 0 10 0 10
  //   12*0 8*8 30 7*0 38 14*0 9*38 20 38*0 38 0 0 38 21*0 30 5*38 0 0 0 38 0 38 20*0 20 5*0 38 153*0 38
  //   48*0 17*10 4*0 6*10 5*0 40 4 2 3 30 20 20 26*0 8 8 8 20 28 28 10*10 4*0 6*10 6*0 38 38 38 0 38 20
  //   29*0 38 0 28 0 18 1 19 1 5 6 7 10 10 4*0 10 0 0 10 0 10 12*0 8*8 30 7*0 38 14*0 9*38 20 38*0 38 0 0
  //   38 21*0 30 38 7*0 38 0 38 20*0 20 5*0 38 153*0 38 48*0 19*10 0 0 6*10 5*0 40 4 2 3 30 20 20 26*0 8 8
  //   8 20 28 28 12*10 0 0 6*10 6*0 38 38 38 0 38 20 29*0 38 0 28 0 18 1 19 1 5 6 7 4*10 0 0 10 0 0 10 0
  //   10 12*0 8*8 30 7*0 38 14*0 9*38 20 38*0 38 0 0 38 21*0 30 38 38 38 5*0 38 0 38 20*0 20 5*0 38 153*0
  //   38 48*0 17*10 0 0 8*10 5*0 40 4 2 3 30 20 20 26*0 8 8 8 20 28 28 10*10 0 0 8*10 6*0 38 38 38 0 38 20
  //   29*0 38 0 28 0 18 1 19 1 5 6 7 10 10 0 0 10 10 10 0 0 10 0 10 12*0 8*8 30 7*0 38 14*0 9*38 20 38*0
  //   38 0 0 38 21*0 30 38 0 0 38 38 0 0 0 38 0 38 20*0 20 5*0 38 153*0 38 48*0 27*10 5*0 40 4 2 3 30 20
  //   20 26*0 8 8 8 20 28 28 20*10 6*0 38 38 38 0 38 20 29*0 38 0 28 0 18 1 19 1 5 6 7 7*10 0 0 10 0 10
  //   12*0 8*8 30 7*0 38 14*0 9*38 20 38*0 38 0 0 38 21*0 30 5*38 0 0 0 38 0 38 20*0 20 5*0 38 153*0 38
endmodule
