// Logisim project fpga.circ as structural Verilog: 4 circuits, main circuit main
module main (
  input  RX0,
  input  L0,
  input  L1,
  input  RX1,
  input  T0,
  input  T1,
  input  R0,
  input  R1,
  input  BX0,
  input  BX1,
  input  B0,
  input  TX0,
  input  B1,
  input  TX1,
  input  LX0,
  input  LX1
);

  wire and_1_out, and_2_out, and_3_out, and_4_out, and_5_out, and_6_out, and_7_out, and_8_out, d_ff_1_q,
       d_ff_2_q, multiplexer_4_out, multiplexer_5_out, multiplexer_6_out, multiplexer_7_out,
       shift_register_1_p1, shift_register_1_p2, shift_register_2_p1, shift_register_2_p3,
       shift_register_2_p4, shift_register_2_p5, shift_register_2_p6, shift_register_2_p7,
       shift_register_2_p8, shift_register_2_p9, shift_register_2_p10, shift_register_2_p11,
       shift_register_2_p12, shift_register_2_p13, shift_register_3_p1, shift_register_3_p2,
       shift_register_3_p3, shift_register_3_p4, shift_register_4_p1, shift_register_4_p2,
       shift_register_4_p3, shift_register_4_p4, shift_register_4_p5, shift_register_4_p6,
       shift_register_4_p7, shift_register_4_p8, shift_register_4_p9, shift_register_4_p10,
       shift_register_4_p11, shift_register_4_p12;
  wire [2:0] multiplexer_1_out;

  // Shift_Register shift_register_1: pin names not known; wires that end beside it: shift_register_1_p1, shift_register_1_p2
  // Shift_Register shift_register_2: pin names not known; wires that end beside it: shift_register_2_p1, shift_register_2_p1, shift_register_2_p3, shift_register_2_p4, shift_register_2_p5, shift_register_2_p6, shift_register_2_p7, shift_register_2_p8, shift_register_2_p9, shift_register_2_p10, shift_register_2_p11, shift_register_2_p12, shift_register_2_p13
  Multiplexer multiplexer_1 (.in0(L0), .in1(L1), .out(multiplexer_1_out[0]), .sel(shift_register_2_p3));
  Multiplexer multiplexer_2 (.in0(T0), .in1(T1), .out(multiplexer_1_out[1]), .sel(shift_register_2_p4));
  Multiplexer multiplexer_3 (.in0(R0), .in1(R1), .out(multiplexer_1_out[2]), .sel(shift_register_2_p5));
  // Shift_Register shift_register_3: pin names not known; wires that end beside it: shift_register_3_p1, shift_register_3_p2, shift_register_3_p3, shift_register_3_p4
  // Shift_Register shift_register_4: pin names not known; wires that end beside it: shift_register_4_p1, shift_register_4_p2, shift_register_4_p3, shift_register_4_p4, shift_register_4_p5, shift_register_4_p6, shift_register_4_p7, shift_register_4_p8, shift_register_4_p9, shift_register_4_p10, shift_register_4_p11, shift_register_4_p12
  D_Flip_Flop d_ff_1 (.D(multiplexer_4_out), .Q(d_ff_1_q));  // open: clk, Qn, preset, reset
  Multiplexer #(.select(3)) multiplexer_4 (
    .in0(shift_register_3_p1), .in1(shift_register_3_p2), .in2(shift_register_3_p3),
    .in3(shift_register_3_p4), .in4(shift_register_4_p1), .in5(shift_register_4_p2),
    .in6(shift_register_4_p3), .in7(shift_register_4_p4), .out(multiplexer_4_out), .sel(multiplexer_1_out));
  D_Flip_Flop d_ff_2 (.D(multiplexer_5_out), .Q(d_ff_2_q));  // open: clk, Qn, preset, reset
  Multiplexer #(.select(3)) multiplexer_5 (
    .in0(shift_register_4_p5), .in1(shift_register_4_p6), .in2(shift_register_4_p7),
    .in3(shift_register_4_p8), .in4(shift_register_4_p9), .in5(shift_register_4_p10),
    .in6(shift_register_4_p11), .in7(shift_register_4_p12), .out(multiplexer_5_out), .sel(multiplexer_1_out));
  Multiplexer multiplexer_6 (
    .in0(multiplexer_4_out), .in1(d_ff_1_q), .out(multiplexer_6_out), .sel(shift_register_1_p1));
  Multiplexer multiplexer_7 (
    .in0(multiplexer_5_out), .in1(d_ff_2_q), .out(multiplexer_7_out), .sel(shift_register_1_p2));
  and and_1 (and_1_out, L0, shift_register_2_p12);
  or or_1 (RX0, and_1_out, and_2_out);
  and and_2 (and_2_out, multiplexer_6_out, shift_register_2_p6);
  and and_3 (and_3_out, multiplexer_6_out, shift_register_2_p7);
  or or_2 (RX1, and_3_out, and_4_out);
  and and_4 (and_4_out, T0, shift_register_2_p13);
  and and_5 (and_5_out, L1, shift_register_2_p10);
  or or_3 (BX0, and_5_out, and_6_out);
  and and_6 (and_6_out, multiplexer_7_out, shift_register_2_p8);
  and and_7 (and_7_out, multiplexer_7_out, shift_register_2_p9);
  or or_4 (BX1, and_7_out, and_8_out);
  and and_8 (and_8_out, T1, shift_register_2_p11);
  and and_9 (TX0, B0, shift_register_2_p10);
  and and_10 (TX1, B1, shift_register_2_p11);
  and and_11 (LX0, R0, shift_register_2_p12);
  and and_12 (LX1, R1, shift_register_2_p13);
endmodule

module test (
  input  L0,
  input  L1,
  input  T0,
  input  T1,
  input  in_5,
  input  R0,
  input  R1,
  input  in_8
);

  wire C, controlled_buffer_1_out, controlled_buffer_2_out, controlled_buffer_3_out, controlled_buffer_4_out,
       controlled_buffer_5_out, controlled_buffer_6_out, d_ff_1_q, d_ff_2_q, multiplexer_4_out,
       multiplexer_5_out, multiplexer_6_out, multiplexer_7_out, not_1_out, not_2_out, not_3_out, not_4_out,
       shift_register_1_p2, shift_register_1_p3, shift_register_1_p4, shift_register_1_p5,
       shift_register_1_p6, shift_register_1_p7, shift_register_1_p8, shift_register_1_p9,
       shift_register_1_p10, shift_register_1_p11, shift_register_1_p12, shift_register_2_p2,
       shift_register_2_p3, shift_register_2_p4, shift_register_2_p5, shift_register_3_p2,
       shift_register_3_p3, shift_register_3_p4, shift_register_3_p5, shift_register_3_p6,
       shift_register_3_p7, shift_register_3_p8, shift_register_3_p9, shift_register_3_p10,
       shift_register_3_p11, shift_register_3_p12, shift_register_3_p13, undriven;
  wire [2:0] multiplexer_1_out;

  Clock clock_1 (.out(C));
  // Shift_Register #(.length(13)) shift_register_1: pin names not known; wires that end beside it: C, shift_register_1_p2, shift_register_1_p3, shift_register_1_p4, shift_register_1_p5, shift_register_1_p6, shift_register_1_p7, shift_register_1_p8, shift_register_1_p9, shift_register_1_p10, shift_register_1_p11, shift_register_1_p12, shift_register_1_p10
  assign controlled_buffer_1_out = not_2_out ? R0 : 1'bz;  // Controlled_Buffer controlled_buffer_1
  assign controlled_buffer_2_out = not_1_out ? R1 : 1'bz;  // Controlled_Buffer controlled_buffer_2
  assign controlled_buffer_3_out = shift_register_1_p10 ? L1 : 1'bz;  // Controlled_Buffer controlled_buffer_3
  assign controlled_buffer_4_out = shift_register_1_p9 ? L0 : 1'bz;  // Controlled_Buffer controlled_buffer_4
  Multiplexer multiplexer_1 (.in0(L0), .in1(L1), .out(multiplexer_1_out[0]), .sel(shift_register_1_p4));
  Multiplexer multiplexer_2 (.in0(T0), .in1(T1), .out(multiplexer_1_out[1]), .sel(shift_register_1_p5));
  Multiplexer multiplexer_3 (
    .in0(controlled_buffer_1_out), .in1(controlled_buffer_2_out), .out(multiplexer_1_out[2]),
    .sel(shift_register_1_p6));
  assign controlled_buffer_5_out = shift_register_1_p7 ? T1 : 1'bz;  // Controlled_Buffer controlled_buffer_5
  assign controlled_buffer_6_out = shift_register_1_p8 ? T0 : 1'bz;  // Controlled_Buffer controlled_buffer_6
  // Shift_Register shift_register_2: pin names not known; wires that end beside it: C, shift_register_2_p2, shift_register_2_p3, shift_register_2_p4, shift_register_2_p5
  // Shift_Register shift_register_3: pin names not known; wires that end beside it: C, shift_register_3_p2, shift_register_3_p3, shift_register_3_p4, shift_register_3_p5, shift_register_3_p6, shift_register_3_p7, shift_register_3_p8, shift_register_3_p9, shift_register_3_p10, shift_register_3_p11, shift_register_3_p12, shift_register_3_p13
  Multiplexer #(.select(3)) multiplexer_4 (
    .in0(shift_register_2_p2), .in1(shift_register_2_p3), .in2(shift_register_2_p4),
    .in3(shift_register_2_p5), .in4(shift_register_3_p2), .in5(shift_register_3_p3),
    .in6(shift_register_3_p4), .in7(shift_register_3_p5), .out(multiplexer_4_out), .sel(multiplexer_1_out));
  Multiplexer #(.select(3)) multiplexer_5 (
    .in0(shift_register_3_p6), .in1(shift_register_3_p7), .in2(shift_register_3_p8),
    .in3(shift_register_3_p9), .in4(shift_register_3_p10), .in5(shift_register_3_p11),
    .in6(shift_register_3_p12), .in7(shift_register_3_p13), .out(multiplexer_5_out), .sel(multiplexer_1_out));
  D_Flip_Flop d_ff_1 (.D(multiplexer_4_out), .clk(C), .Q(d_ff_1_q));  // open: Qn, preset, reset
  D_Flip_Flop d_ff_2 (.D(multiplexer_5_out), .clk(C), .Q(d_ff_2_q));  // open: Qn, preset, reset
  assign controlled_buffer_4_out = shift_register_1_p10 ? multiplexer_6_out : 1'bz;  // Controlled_Buffer controlled_buffer_7
  Multiplexer multiplexer_6 (
    .in0(multiplexer_4_out), .in1(d_ff_1_q), .out(multiplexer_6_out), .sel(shift_register_1_p2));
  assign controlled_buffer_3_out = undriven ? multiplexer_6_out : 1'bz;  // Controlled_Buffer controlled_buffer_8
  assign controlled_buffer_2_out = not_3_out ? controlled_buffer_3_out : 1'bz;  // Controlled_Buffer controlled_buffer_9
  not not_1 (not_1_out, in_5);
  assign controlled_buffer_1_out = not_4_out ? controlled_buffer_4_out : 1'bz;  // Controlled_Buffer controlled_buffer_10
  not not_2 (not_2_out, in_8);
  assign controlled_buffer_6_out = shift_register_1_p12 ? multiplexer_7_out : 1'bz;  // Controlled_Buffer controlled_buffer_11
  Multiplexer multiplexer_7 (
    .in0(multiplexer_5_out), .in1(d_ff_2_q), .out(multiplexer_7_out), .sel(shift_register_1_p3));
  assign controlled_buffer_5_out = shift_register_1_p11 ? multiplexer_7_out : 1'bz;  // Controlled_Buffer controlled_buffer_12
  assign controlled_buffer_3_out = not_1_out ? controlled_buffer_2_out : 1'bz;  // Controlled_Buffer controlled_buffer_13
  not not_3 (not_3_out, not_1_out);
  assign controlled_buffer_4_out = not_2_out ? controlled_buffer_1_out : 1'bz;  // Controlled_Buffer controlled_buffer_14
  not not_4 (not_4_out, not_2_out);
endmodule

module clb (
  input  CLK,
  input  RST,
  input  L0,
  input  L1,
  input  T0,
  input  T1,
  input  R0,
  input  R1,
  input  C0,
  input  C1,
  input  C2,
  input  C3,
  input  C4,
  input  C5,
  input  C6,
  input  C7,
  input  C8,
  input  SE0,
  input  S0,
  input  SE1,
  input  S1,
  output RX0,
  output RX1,
  output BX0,
  output BX1
);

  wire d_ff_1_q, d_ff_2_q, multiplexer_4_out, multiplexer_5_out, multiplexer_6_out, multiplexer_7_out,
       shift_register_1_p5, shift_register_1_p6, shift_register_1_p7, shift_register_1_p8,
       shift_register_2_p5, shift_register_2_p6, shift_register_2_p7, shift_register_2_p8,
       shift_register_2_p9, shift_register_2_p10, shift_register_2_p11, shift_register_2_p12,
       shift_register_2_p13, shift_register_2_p14, shift_register_2_p15, shift_register_2_p16;
  wire [2:0] multiplexer_1_out;

  Multiplexer multiplexer_1 (.in0(L0), .in1(L1), .out(multiplexer_1_out[0]), .sel(C0));
  Multiplexer multiplexer_2 (.in0(T0), .in1(T1), .out(multiplexer_1_out[1]), .sel(C1));
  Multiplexer multiplexer_3 (.in0(R0), .in1(R1), .out(multiplexer_1_out[2]), .sel(C2));
  // Shift_Register shift_register_1: pin names not known; wires that end beside it: RST, SE0, CLK, S0, shift_register_1_p5, shift_register_1_p6, shift_register_1_p7, shift_register_1_p8
  // Shift_Register shift_register_2: pin names not known; wires that end beside it: RST, SE1, CLK, S1, shift_register_2_p5, shift_register_2_p6, shift_register_2_p7, shift_register_2_p8, shift_register_2_p9, shift_register_2_p10, shift_register_2_p11, shift_register_2_p12, shift_register_2_p13, shift_register_2_p14, shift_register_2_p15, shift_register_2_p16
  Multiplexer #(.select(3)) multiplexer_4 (
    .in0(shift_register_1_p5), .in1(shift_register_1_p6), .in2(shift_register_1_p7),
    .in3(shift_register_1_p8), .in4(shift_register_2_p5), .in5(shift_register_2_p6),
    .in6(shift_register_2_p7), .in7(shift_register_2_p8), .out(multiplexer_4_out), .sel(multiplexer_1_out));
  Multiplexer #(.select(3)) multiplexer_5 (
    .in0(shift_register_2_p9), .in1(shift_register_2_p10), .in2(shift_register_2_p11),
    .in3(shift_register_2_p12), .in4(shift_register_2_p13), .in5(shift_register_2_p14),
    .in6(shift_register_2_p15), .in7(shift_register_2_p16), .out(multiplexer_5_out), .sel(multiplexer_1_out));
  D_Flip_Flop d_ff_1 (.D(multiplexer_4_out), .clk(CLK), .Q(d_ff_1_q));  // open: Qn, preset, reset
  D_Flip_Flop d_ff_2 (.D(multiplexer_5_out), .clk(CLK), .Q(d_ff_2_q));  // open: Qn, preset, reset
  assign RX0 = C5 ? multiplexer_6_out : 1'bz;  // Controlled_Buffer controlled_buffer_1
  Multiplexer multiplexer_6 (.in0(multiplexer_4_out), .in1(d_ff_1_q), .out(multiplexer_6_out), .sel(C3));
  assign RX1 = C6 ? multiplexer_6_out : 1'bz;  // Controlled_Buffer controlled_buffer_2
  assign BX0 = C7 ? multiplexer_7_out : 1'bz;  // Controlled_Buffer controlled_buffer_3
  Multiplexer multiplexer_7 (.in0(multiplexer_5_out), .in1(d_ff_2_q), .out(multiplexer_7_out), .sel(C4));
  assign BX1 = C8 ? multiplexer_7_out : 1'bz;  // Controlled_Buffer controlled_buffer_4

  // Other names for the same wires on the sheet: C = CLK
endmodule

module slice (
);

  wire clb_1_bx0, clb_1_bx1, clb_1_rx0, clb_1_rx1, clb_2_rx0, clb_3_bx0, clb_3_bx1, clb_3_rx0, clb_3_rx1,
       clb_4_rx0, clb_5_bx0, clb_5_bx1;

  clb clb_1 (
    .R0(clb_1_rx0), .R1(clb_1_rx1), .RX0(clb_1_rx0), .RX1(clb_1_rx1), .BX0(clb_1_bx0), .BX1(clb_1_bx1));  // open: CLK, RST, L0, L1, T0, T1, C0, C1, C2, C3, C4, C5, C6, C7, C8, SE0, S0, SE1, S1
  clb clb_2 (
    .T0(clb_1_bx0), .T1(clb_1_bx1), .R0(clb_2_rx0), .R1(clb_2_rx0), .RX0(clb_2_rx0), .RX1(clb_2_rx0));  // open: CLK, RST, L0, L1, C0, C1, C2, C3, C4, C5, C6, C7, C8, SE0, S0, SE1, S1, BX0, BX1
  clb clb_3 (
    .L0(clb_1_rx0), .L1(clb_1_rx1), .R0(clb_3_rx0), .R1(clb_3_rx1), .RX0(clb_3_rx0), .RX1(clb_3_rx1),
    .BX0(clb_3_bx0), .BX1(clb_3_bx1));  // open: CLK, RST, T0, T1, C0, C1, C2, C3, C4, C5, C6, C7, C8, SE0, S0, SE1, S1
  clb clb_4 (
    .L0(clb_2_rx0), .L1(clb_2_rx0), .T0(clb_3_bx0), .T1(clb_3_bx1), .R0(clb_4_rx0), .R1(clb_4_rx0),
    .RX0(clb_4_rx0), .RX1(clb_4_rx0));  // open: CLK, RST, C0, C1, C2, C3, C4, C5, C6, C7, C8, SE0, S0, SE1, S1, BX0, BX1
  clb clb_5 (
    .L0(clb_3_rx0), .L1(clb_3_rx1), .BX0(clb_5_bx0), .BX1(clb_5_bx1));  // open: CLK, RST, T0, T1, R0, R1, C0, C1, C2, C3, C4, C5, C6, C7, C8, SE0, S0, SE1, S1, RX0, RX1
  clb clb_6 (
    .L0(clb_4_rx0), .L1(clb_4_rx0), .T0(clb_5_bx0), .T1(clb_5_bx1));  // open: CLK, RST, R0, R1, C0, C1, C2, C3, C4, C5, C6, C7, C8, SE0, S0, SE1, S1, RX0, RX1, BX0, BX1
endmodule
